// Logisim project Project.circ as structural Verilog: 28 circuits, main circuit main
module main (
  input  [15:0] A,
  input  [15:0] B,
  output Great,
  output Equal,
  output Less
);

  wire bitcomparator_1_eout, bitcomparator_1_gout, bitcomparator_2_eout, bitcomparator_2_gout,
       bitcomparator_3_eout, bitcomparator_3_gout, bitcomparator_4_eout, bitcomparator_4_gout,
       bitcomparator_5_eout, bitcomparator_5_gout, bitcomparator_6_eout, bitcomparator_6_gout,
       bitcomparator_7_eout, bitcomparator_7_gout, bitcomparator_8_eout, bitcomparator_8_gout,
       bitcomparator_9_eout, bitcomparator_9_gout, bitcomparator_10_eout, bitcomparator_10_gout,
       bitcomparator_11_eout, bitcomparator_11_gout, bitcomparator_12_eout, bitcomparator_12_gout,
       bitcomparator_13_eout, bitcomparator_13_gout, bitcomparator_14_eout, bitcomparator_14_gout,
       bitcomparator_15_eout, bitcomparator_15_gout, bitcomparator_16_eout, bitcomparator_16_gout, not_1_out,
       xor_1_out;

  BitComparator bitcomparator_1 (
    .A(A[0]), .B(B[0]), .E(bitcomparator_2_eout), .G(bitcomparator_2_gout), .Gout(bitcomparator_1_gout),
    .Eout(bitcomparator_1_eout));
  BitComparator bitcomparator_2 (
    .A(A[1]), .B(B[1]), .E(bitcomparator_3_eout), .G(bitcomparator_3_gout), .Gout(bitcomparator_2_gout),
    .Eout(bitcomparator_2_eout));
  BitComparator bitcomparator_3 (
    .A(A[2]), .B(B[2]), .E(bitcomparator_4_eout), .G(bitcomparator_4_gout), .Gout(bitcomparator_3_gout),
    .Eout(bitcomparator_3_eout));
  BitComparator bitcomparator_4 (
    .A(A[3]), .B(B[3]), .E(bitcomparator_5_eout), .G(bitcomparator_5_gout), .Gout(bitcomparator_4_gout),
    .Eout(bitcomparator_4_eout));
  BitComparator bitcomparator_5 (
    .A(A[4]), .B(B[4]), .E(bitcomparator_6_eout), .G(bitcomparator_6_gout), .Gout(bitcomparator_5_gout),
    .Eout(bitcomparator_5_eout));
  BitComparator bitcomparator_6 (
    .A(A[5]), .B(B[5]), .E(bitcomparator_7_eout), .G(bitcomparator_7_gout), .Gout(bitcomparator_6_gout),
    .Eout(bitcomparator_6_eout));
  BitComparator bitcomparator_7 (
    .A(A[6]), .B(B[6]), .E(bitcomparator_8_eout), .G(bitcomparator_8_gout), .Gout(bitcomparator_7_gout),
    .Eout(bitcomparator_7_eout));
  BitComparator bitcomparator_8 (
    .A(A[7]), .B(B[7]), .E(bitcomparator_9_eout), .G(bitcomparator_9_gout), .Gout(bitcomparator_8_gout),
    .Eout(bitcomparator_8_eout));
  BitComparator bitcomparator_9 (
    .A(A[8]), .B(B[8]), .E(bitcomparator_10_eout), .G(bitcomparator_10_gout), .Gout(bitcomparator_9_gout),
    .Eout(bitcomparator_9_eout));
  BitComparator bitcomparator_10 (
    .A(A[9]), .B(B[9]), .E(bitcomparator_11_eout), .G(bitcomparator_11_gout), .Gout(bitcomparator_10_gout),
    .Eout(bitcomparator_10_eout));
  BitComparator bitcomparator_11 (
    .A(A[10]), .B(B[10]), .E(bitcomparator_12_eout), .G(bitcomparator_12_gout), .Gout(bitcomparator_11_gout),
    .Eout(bitcomparator_11_eout));
  BitComparator bitcomparator_12 (
    .A(A[11]), .B(B[11]), .E(bitcomparator_13_eout), .G(bitcomparator_13_gout), .Gout(bitcomparator_12_gout),
    .Eout(bitcomparator_12_eout));
  BitComparator bitcomparator_13 (
    .A(A[12]), .B(B[12]), .E(bitcomparator_14_eout), .G(bitcomparator_14_gout), .Gout(bitcomparator_13_gout),
    .Eout(bitcomparator_13_eout));
  BitComparator bitcomparator_14 (
    .A(A[13]), .B(B[13]), .E(bitcomparator_15_eout), .G(bitcomparator_15_gout), .Gout(bitcomparator_14_gout),
    .Eout(bitcomparator_14_eout));
  BitComparator bitcomparator_15 (
    .A(A[14]), .B(B[14]), .E(bitcomparator_16_eout), .G(bitcomparator_16_gout), .Gout(bitcomparator_15_gout),
    .Eout(bitcomparator_15_eout));
  BitComparator bitcomparator_16 (
    .A(A[15]), .B(B[15]), .E(1'b1), .G(1'b0), .Gout(bitcomparator_16_gout), .Eout(bitcomparator_16_eout));
  not not_1 (not_1_out, bitcomparator_1_gout);
  xor xor_1 (xor_1_out, A[15], B[15]);
  Multiplexer multiplexer_1 (.in0(bitcomparator_1_gout), .in1(not_1_out), .out(Great), .sel(xor_1_out));
  AND16 and16_1 (
    .in_1(bitcomparator_1_eout), .in_2(bitcomparator_2_eout), .in_3(bitcomparator_3_eout),
    .in_4(bitcomparator_4_eout), .in_5(bitcomparator_5_eout), .in_6(bitcomparator_6_eout),
    .in_7(bitcomparator_7_eout), .in_8(bitcomparator_8_eout), .in_9(bitcomparator_9_eout),
    .in_10(bitcomparator_10_eout), .in_11(bitcomparator_11_eout), .in_12(bitcomparator_12_eout),
    .in_13(bitcomparator_13_eout), .in_14(bitcomparator_14_eout), .in_15(bitcomparator_15_eout),
    .in_16(bitcomparator_16_eout), .out_17(Equal));
  nor nor_1 (Less, Great, Equal);
endmodule

module BitComparator (
  input  A,
  input  B,
  input  E,
  input  G,
  output Gout,
  output Eout
);

  wire and_1_out, and_2_out, not_1_out, xnor_1_out;

  not not_1 (not_1_out, B);
  and and_1 (and_1_out, A, not_1_out);
  and and_2 (and_2_out, and_1_out, E);
  xnor xnor_1 (xnor_1_out, A, B);
  or or_1 (Gout, and_2_out, G);
  and and_3 (Eout, xnor_1_out, E);
endmodule

module AND16 (
  input  in_1,
  input  in_2,
  input  in_3,
  input  in_4,
  input  in_5,
  input  in_6,
  input  in_7,
  input  in_8,
  input  in_9,
  input  in_10,
  input  in_11,
  input  in_12,
  input  in_13,
  input  in_14,
  input  in_15,
  input  in_16,
  output out_17
);

  wire and_1_out, and_2_out, and_3_out, and_4_out, and_5_out, and_6_out, and_7_out, and_8_out, and_9_out,
       and_10_out, and_11_out, and_12_out, and_13_out, and_14_out;

  and and_1 (and_1_out, in_15, in_16);
  and and_2 (and_2_out, in_14, and_1_out);
  and and_3 (and_3_out, in_13, and_2_out);
  and and_4 (and_4_out, in_12, and_3_out);
  and and_5 (and_5_out, in_11, and_4_out);
  and and_6 (and_6_out, in_9, and_7_out);
  and and_7 (and_7_out, in_10, and_5_out);
  and and_8 (and_8_out, in_8, and_6_out);
  and and_9 (and_9_out, in_7, and_8_out);
  and and_10 (and_10_out, in_6, and_9_out);
  and and_11 (and_11_out, in_5, and_10_out);
  and and_12 (and_12_out, in_3, and_13_out);
  and and_13 (and_13_out, in_4, and_11_out);
  and and_14 (and_14_out, in_2, and_12_out);
  and and_15 (out_17, in_1, and_14_out);
endmodule

module Comparator16Bit (
  input  [15:0] A,
  input  [15:0] B,
  output Great,
  output Equal,
  output Less
);

  wire bitcomparator_1_eout, bitcomparator_1_gout, bitcomparator_2_eout, bitcomparator_2_gout,
       bitcomparator_3_eout, bitcomparator_3_gout, bitcomparator_4_eout, bitcomparator_4_gout,
       bitcomparator_5_eout, bitcomparator_5_gout, bitcomparator_6_eout, bitcomparator_6_gout,
       bitcomparator_7_eout, bitcomparator_7_gout, bitcomparator_8_eout, bitcomparator_8_gout,
       bitcomparator_9_eout, bitcomparator_9_gout, bitcomparator_10_eout, bitcomparator_10_gout,
       bitcomparator_11_eout, bitcomparator_11_gout, bitcomparator_12_eout, bitcomparator_12_gout,
       bitcomparator_13_eout, bitcomparator_13_gout, bitcomparator_14_eout, bitcomparator_14_gout,
       bitcomparator_15_eout, bitcomparator_15_gout, bitcomparator_16_eout, bitcomparator_16_gout, not_1_out,
       xor_1_out;

  BitComparator bitcomparator_1 (
    .A(A[0]), .B(B[0]), .E(bitcomparator_2_eout), .G(bitcomparator_2_gout), .Gout(bitcomparator_1_gout),
    .Eout(bitcomparator_1_eout));
  BitComparator bitcomparator_2 (
    .A(A[1]), .B(B[1]), .E(bitcomparator_3_eout), .G(bitcomparator_3_gout), .Gout(bitcomparator_2_gout),
    .Eout(bitcomparator_2_eout));
  BitComparator bitcomparator_3 (
    .A(A[2]), .B(B[2]), .E(bitcomparator_4_eout), .G(bitcomparator_4_gout), .Gout(bitcomparator_3_gout),
    .Eout(bitcomparator_3_eout));
  BitComparator bitcomparator_4 (
    .A(A[3]), .B(B[3]), .E(bitcomparator_5_eout), .G(bitcomparator_5_gout), .Gout(bitcomparator_4_gout),
    .Eout(bitcomparator_4_eout));
  BitComparator bitcomparator_5 (
    .A(A[4]), .B(B[4]), .E(bitcomparator_6_eout), .G(bitcomparator_6_gout), .Gout(bitcomparator_5_gout),
    .Eout(bitcomparator_5_eout));
  BitComparator bitcomparator_6 (
    .A(A[5]), .B(B[5]), .E(bitcomparator_7_eout), .G(bitcomparator_7_gout), .Gout(bitcomparator_6_gout),
    .Eout(bitcomparator_6_eout));
  BitComparator bitcomparator_7 (
    .A(A[6]), .B(B[6]), .E(bitcomparator_8_eout), .G(bitcomparator_8_gout), .Gout(bitcomparator_7_gout),
    .Eout(bitcomparator_7_eout));
  BitComparator bitcomparator_8 (
    .A(A[7]), .B(B[7]), .E(bitcomparator_9_eout), .G(bitcomparator_9_gout), .Gout(bitcomparator_8_gout),
    .Eout(bitcomparator_8_eout));
  BitComparator bitcomparator_9 (
    .A(A[8]), .B(B[8]), .E(bitcomparator_10_eout), .G(bitcomparator_10_gout), .Gout(bitcomparator_9_gout),
    .Eout(bitcomparator_9_eout));
  BitComparator bitcomparator_10 (
    .A(A[9]), .B(B[9]), .E(bitcomparator_11_eout), .G(bitcomparator_11_gout), .Gout(bitcomparator_10_gout),
    .Eout(bitcomparator_10_eout));
  BitComparator bitcomparator_11 (
    .A(A[10]), .B(B[10]), .E(bitcomparator_12_eout), .G(bitcomparator_12_gout), .Gout(bitcomparator_11_gout),
    .Eout(bitcomparator_11_eout));
  BitComparator bitcomparator_12 (
    .A(A[11]), .B(B[11]), .E(bitcomparator_13_eout), .G(bitcomparator_13_gout), .Gout(bitcomparator_12_gout),
    .Eout(bitcomparator_12_eout));
  BitComparator bitcomparator_13 (
    .A(A[12]), .B(B[12]), .E(bitcomparator_14_eout), .G(bitcomparator_14_gout), .Gout(bitcomparator_13_gout),
    .Eout(bitcomparator_13_eout));
  BitComparator bitcomparator_14 (
    .A(A[13]), .B(B[13]), .E(bitcomparator_15_eout), .G(bitcomparator_15_gout), .Gout(bitcomparator_14_gout),
    .Eout(bitcomparator_14_eout));
  BitComparator bitcomparator_15 (
    .A(A[14]), .B(B[14]), .E(bitcomparator_16_eout), .G(bitcomparator_16_gout), .Gout(bitcomparator_15_gout),
    .Eout(bitcomparator_15_eout));
  BitComparator bitcomparator_16 (
    .A(A[15]), .B(B[15]), .E(1'b1), .G(1'b0), .Gout(bitcomparator_16_gout), .Eout(bitcomparator_16_eout));
  not not_1 (not_1_out, bitcomparator_1_gout);
  xor xor_1 (xor_1_out, A[15], B[15]);
  Multiplexer multiplexer_1 (.in0(bitcomparator_1_gout), .in1(not_1_out), .out(Great), .sel(xor_1_out));
  AND16 and16_1 (
    .in_1(bitcomparator_1_eout), .in_2(bitcomparator_2_eout), .in_3(bitcomparator_3_eout),
    .in_4(bitcomparator_4_eout), .in_5(bitcomparator_5_eout), .in_6(bitcomparator_6_eout),
    .in_7(bitcomparator_7_eout), .in_8(bitcomparator_8_eout), .in_9(bitcomparator_9_eout),
    .in_10(bitcomparator_10_eout), .in_11(bitcomparator_11_eout), .in_12(bitcomparator_12_eout),
    .in_13(bitcomparator_13_eout), .in_14(bitcomparator_14_eout), .in_15(bitcomparator_15_eout),
    .in_16(bitcomparator_16_eout), .out_17(Equal));
  nor nor_1 (Less, Great, Equal);
endmodule

module ALU (
  input  [15:0] A,
  input  [15:0] B,
  input  [2:0] Selector,
  output P,
  output Z,
  output N,
  output [15:0] Result,
  output Overflow
);

  wire adder16bits_1_c_out, adder16bits_1_penult_carry_out, comparator16bit_1_equal, or_1_out,
       subs16bits_1_cout, subs16bits_1_pcarry, xor_1_out, xor_2_out;
  wire [15:0] adder16bits_1_sum, and16bitwise_1_r, not16bitwise_1_r, not16bitwise_2_r, or16bitwise_1_r,
       subs16bits_1_r;

  Adder16Bits adder16bits_1 (
    .A(A), .B(B), .C_Out(adder16bits_1_c_out), .penult_carry_out(adder16bits_1_penult_carry_out),
    .Sum(adder16bits_1_sum));
  xor xor_1 (xor_1_out, adder16bits_1_c_out, adder16bits_1_penult_carry_out);
  subs16Bits subs16bits_1 (.A(A), .B(B), .R(subs16bits_1_r), .Cout(subs16bits_1_cout), .Pcarry(subs16bits_1_pcarry));
  xor xor_2 (xor_2_out, subs16bits_1_pcarry, subs16bits_1_cout);
  or or_1 (or_1_out, xor_2_out, comparator16bit_1_equal);
  AND16Bitwise and16bitwise_1 (.A(A), .B(B), .R(and16bitwise_1_r));
  mux8x3 mux8x3_1 (
    .S(Selector), .A(xor_1_out), .B(or_1_out), .C(1'b0), .D(1'b0), .E(1'b0), .F(1'b0), .G(1'b0), .H(1'b0),
    .o(Overflow));
  OR16Bitwise or16bitwise_1 (.A(A), .B(B), .R(or16bitwise_1_r));
  Multiplexer #(.select(3), .width(16)) multiplexer_1 (
    .in0(adder16bits_1_sum), .in1(subs16bits_1_r), .in2(and16bitwise_1_r), .in3(or16bitwise_1_r),
    .in4(not16bitwise_1_r), .in5(not16bitwise_2_r), .in6(A), .in7(B), .out(Result), .sel(Selector));
  Comparator16Bit comparator16bit_1 (.A(B), .B(16'h8000), .Equal(comparator16bit_1_equal));  // open: Less, Great
  NOT16Bitwise not16bitwise_1 (.A(A), .R(not16bitwise_1_r));
  Comparator16Bit comparator16bit_2 (.A(Result), .B({16{1'b0}}), .Less(N), .Great(P), .Equal(Z));
  NOT16Bitwise not16bitwise_2 (.A(B), .R(not16bitwise_2_r));

  // Notes on the sheet:
  //   0 : Suma
  //   1 : Resta
  //   2 :AND Bitwise
  //   3 :OR Bitwise
  //   4 :NOT A
  //   5 :NOT B
  //   6: A
  //   7: B
endmodule

module bitAdd (
  input  A,
  input  B,
  input  CarryIn,
  output Sum,
  output CarryOut
);

  wire and_1_out, and_2_out, xor_1_out;

  xor xor_1 (xor_1_out, A, B);
  and and_1 (and_1_out, xor_1_out, CarryIn);
  and and_2 (and_2_out, A, B);
  xor xor_2 (Sum, xor_1_out, CarryIn);
  or or_1 (CarryOut, and_1_out, and_2_out);
endmodule

module Adder16Bits (
  input  [15:0] A,
  input  [15:0] B,
  output C_Out,
  output penult_carry_out,
  output [15:0] Sum
);

  wire N00_carryout, N01_carryout, N02_carryout, N03_carryout, N04_carryout, N05_carryout, N06_carryout,
       N07_carryout, N08_carryout, N09_carryout, N10_carryout, N11_carryout, N12_carryout, N13_carryout;

  bitAdd N15 (.B(A[15]), .CarryIn(penult_carry_out), .A(B[15]), .Sum(Sum[15]), .CarryOut(C_Out));
  bitAdd N14 (.B(A[14]), .CarryIn(N13_carryout), .A(B[14]), .Sum(Sum[14]), .CarryOut(penult_carry_out));
  bitAdd N13 (.B(A[13]), .CarryIn(N12_carryout), .A(B[13]), .Sum(Sum[13]), .CarryOut(N13_carryout));
  bitAdd N12 (.B(A[12]), .CarryIn(N11_carryout), .A(B[12]), .Sum(Sum[12]), .CarryOut(N12_carryout));
  bitAdd N11 (.B(A[11]), .CarryIn(N10_carryout), .A(B[11]), .Sum(Sum[11]), .CarryOut(N11_carryout));
  bitAdd N10 (.B(A[10]), .CarryIn(N09_carryout), .A(B[10]), .Sum(Sum[10]), .CarryOut(N10_carryout));
  bitAdd N09 (.B(A[9]), .CarryIn(N08_carryout), .A(B[9]), .Sum(Sum[9]), .CarryOut(N09_carryout));
  bitAdd N08 (.B(A[8]), .CarryIn(N07_carryout), .A(B[8]), .Sum(Sum[8]), .CarryOut(N08_carryout));
  bitAdd N07 (.B(A[7]), .CarryIn(N06_carryout), .A(B[7]), .Sum(Sum[7]), .CarryOut(N07_carryout));
  bitAdd N06 (.B(A[6]), .CarryIn(N05_carryout), .A(B[6]), .Sum(Sum[6]), .CarryOut(N06_carryout));
  bitAdd N05 (.B(A[5]), .CarryIn(N04_carryout), .A(B[5]), .Sum(Sum[5]), .CarryOut(N05_carryout));
  bitAdd N04 (.B(A[4]), .CarryIn(N03_carryout), .A(B[4]), .Sum(Sum[4]), .CarryOut(N04_carryout));
  bitAdd N03 (.B(A[3]), .CarryIn(N02_carryout), .A(B[3]), .Sum(Sum[3]), .CarryOut(N03_carryout));
  bitAdd N02 (.B(A[2]), .CarryIn(N01_carryout), .A(B[2]), .Sum(Sum[2]), .CarryOut(N02_carryout));
  bitAdd N01 (.B(A[1]), .CarryIn(N00_carryout), .A(B[1]), .Sum(Sum[1]), .CarryOut(N01_carryout));
  bitAdd N00 (.B(A[0]), .A(B[0]), .Sum(Sum[0]), .CarryOut(N00_carryout));  // open: CarryIn
endmodule

module AND16Bitwise (
  input  [15:0] A,
  input  [15:0] B,
  output [15:0] R
);

  and and_1 (R[15], B[15], A[15]);
  and and_2 (R[14], B[14], A[14]);
  and and_3 (R[13], B[13], A[13]);
  and and_4 (R[12], B[12], A[12]);
  and and_5 (R[11], B[11], A[11]);
  and and_6 (R[10], B[10], A[10]);
  and and_7 (R[9], B[9], A[9]);
  and and_8 (R[8], B[8], A[8]);
  and and_9 (R[7], B[7], A[7]);
  and and_10 (R[6], B[6], A[6]);
  and and_11 (R[5], B[5], A[5]);
  and and_12 (R[4], B[4], A[4]);
  and and_13 (R[3], B[3], A[3]);
  and and_14 (R[2], B[2], A[2]);
  and and_15 (R[1], B[1], A[1]);
  and and_16 (R[0], B[0], A[0]);
endmodule

module OR16Bitwise (
  input  [15:0] A,
  input  [15:0] B,
  output [15:0] R
);

  or or_1 (R[15], B[15], A[15]);
  or or_2 (R[14], B[14], A[14]);
  or or_3 (R[13], B[13], A[13]);
  or or_4 (R[12], B[12], A[12]);
  or or_5 (R[11], B[11], A[11]);
  or or_6 (R[10], B[10], A[10]);
  or or_7 (R[9], B[9], A[9]);
  or or_8 (R[8], B[8], A[8]);
  or or_9 (R[7], B[7], A[7]);
  or or_10 (R[6], B[6], A[6]);
  or or_11 (R[5], B[5], A[5]);
  or or_12 (R[4], B[4], A[4]);
  or or_13 (R[3], B[3], A[3]);
  or or_14 (R[2], B[2], A[2]);
  or or_15 (R[1], B[1], A[1]);
  or or_16 (R[0], B[0], A[0]);
endmodule

module XOR16Bitwise (
  input  [15:0] A,
  input  [15:0] B,
  output [15:0] R
);

  xor xor_1 (R[15], B[15], A[15]);
  xor xor_2 (R[14], B[14], A[14]);
  xor xor_3 (R[13], B[13], A[13]);
  xor xor_4 (R[12], B[12], A[12]);
  xor xor_5 (R[11], B[11], A[11]);
  xor xor_6 (R[10], B[10], A[10]);
  xor xor_7 (R[9], B[9], A[9]);
  xor xor_8 (R[8], B[8], A[8]);
  xor xor_9 (R[7], B[7], A[7]);
  xor xor_10 (R[6], B[6], A[6]);
  xor xor_11 (R[5], B[5], A[5]);
  xor xor_12 (R[4], B[4], A[4]);
  xor xor_13 (R[3], B[3], A[3]);
  xor xor_14 (R[2], B[2], A[2]);
  xor xor_15 (R[1], B[1], A[1]);
  xor xor_16 (R[0], B[0], A[0]);
endmodule

module NOT16Bitwise (
  input  [15:0] A,
  output [15:0] R
);

  not not_1 (R[15], A[15]);
  not not_2 (R[14], A[14]);
  not not_3 (R[13], A[13]);
  not not_4 (R[12], A[12]);
  not not_5 (R[11], A[11]);
  not not_6 (R[10], A[10]);
  not not_7 (R[9], A[9]);
  not not_8 (R[8], A[8]);
  not not_9 (R[7], A[7]);
  not not_10 (R[6], A[6]);
  not not_11 (R[5], A[5]);
  not not_12 (R[4], A[4]);
  not not_13 (R[3], A[3]);
  not not_14 (R[2], A[2]);
  not not_15 (R[1], A[1]);
  not not_16 (R[0], A[0]);
endmodule

module subs16Bits (
  input  [15:0] A,
  input  [15:0] B,
  output Cout,
  output Pcarry,
  output [15:0] R
);

  wire [15:0] adder16bits_2_sum, xor16bitwise_1_r;

  Adder16Bits adder16bits_1 (.A(A), .B(adder16bits_2_sum), .C_Out(Cout), .penult_carry_out(Pcarry), .Sum(R));
  Adder16Bits adder16bits_2 (
    .A(16'h1), .B(xor16bitwise_1_r), .Sum(adder16bits_2_sum));  // open: C_Out, penult_carry_out
  XOR16Bitwise xor16bitwise_1 (.A({16{1'b1}}), .B(B), .R(xor16bitwise_1_r));
endmodule

module mux2x1 (
  input  A,
  input  B,
  input  S,
  output out_4
);

  wire and_1_out, and_2_out, not_1_out;

  not not_1 (not_1_out, S);
  and and_1 (and_1_out, A, not_1_out);
  and and_2 (and_2_out, B, S);
  or or_1 (out_4, and_1_out, and_2_out);
endmodule

module mux8x3 (
  input  A,
  input  B,
  input  C,
  input  D,
  input  E,
  input  F,
  input  G,
  input  H,
  input  [2:0] S,
  output o
);

  wire and_1_out, and_2_out, and_3_out, and_4_out, and_5_out, and_6_out, and_7_out, and_8_out, and_9_out,
       and_10_out, and_11_out, and_12_out, and_13_out, and_14_out, and_15_out, and_16_out, and_17_out,
       and_18_out, and_19_out, and_20_out, and_21_out, and_22_out, and_23_out, and_24_out, not_1_out,
       not_2_out, not_3_out, not_4_out, not_5_out, not_6_out, not_7_out, not_8_out, not_9_out, not_10_out,
       not_11_out, not_12_out, or_1_out, or_2_out, or_3_out, or_4_out, or_5_out, or_6_out;

  not not_1 (not_1_out, S[0]);
  not not_2 (not_2_out, S[0]);
  not not_3 (not_3_out, S[0]);
  not not_4 (not_4_out, S[0]);
  and and_1 (and_1_out, A, not_1_out);
  not not_5 (not_5_out, S[1]);
  and and_2 (and_2_out, B, S[0]);
  not not_6 (not_6_out, S[1]);
  and and_3 (and_3_out, C, not_2_out);
  and and_4 (and_4_out, D, S[0]);
  and and_5 (and_5_out, E, not_3_out);
  not not_7 (not_7_out, S[1]);
  and and_6 (and_6_out, F, S[0]);
  not not_8 (not_8_out, S[1]);
  and and_7 (and_7_out, G, not_4_out);
  and and_8 (and_8_out, H, S[0]);
  and and_9 (and_9_out, and_1_out, not_5_out);
  and and_10 (and_10_out, and_2_out, not_6_out);
  and and_11 (and_11_out, and_3_out, S[1]);
  and and_12 (and_12_out, and_4_out, S[1]);
  and and_13 (and_13_out, and_5_out, not_7_out);
  and and_14 (and_14_out, and_6_out, not_8_out);
  and and_15 (and_15_out, and_7_out, S[1]);
  and and_16 (and_16_out, and_8_out, S[1]);
  and and_17 (and_17_out, and_9_out, not_9_out);
  not not_9 (not_9_out, S[2]);
  and and_18 (and_18_out, and_10_out, not_10_out);
  not not_10 (not_10_out, S[2]);
  and and_19 (and_19_out, and_11_out, not_11_out);
  not not_11 (not_11_out, S[2]);
  and and_20 (and_20_out, and_12_out, not_12_out);
  not not_12 (not_12_out, S[2]);
  and and_21 (and_21_out, and_13_out, S[2]);
  buf and_22 (and_22_out, and_14_out);  // AND_Gate
  and and_23 (and_23_out, and_15_out, S[2]);
  and and_24 (and_24_out, and_16_out, S[2]);
  or or_1 (or_1_out, and_17_out, and_18_out);
  or or_2 (or_2_out, and_19_out, and_20_out);
  or or_3 (or_3_out, and_21_out, and_22_out);
  or or_4 (or_4_out, and_23_out, and_24_out);
  or or_5 (or_5_out, or_1_out, or_2_out);
  or or_6 (or_6_out, or_3_out, or_4_out);
  or or_7 (o, or_5_out, or_6_out);
endmodule

module mux8x316Bits (
  input  [2:0] in_1,
  input  [15:0] in_2,
  input  [15:0] in_3,
  input  [15:0] in_4,
  input  [15:0] in_5,
  input  [15:0] in_6,
  input  [15:0] in_7,
  input  [15:0] in_8,
  input  [15:0] in_9
);

  mux8x3 mux8x3_1 (.A(in_2[0]), .B(in_3[0]));  // open: S, C, D, E, F, G, H, o
  mux8x3 mux8x3_2 ();  // open: S, A, B, C, D, E, F, G, H, o
endmodule

module testComparator (
  input  [15:0] in_1,
  input  [15:0] in_2,
  input  [15:0] in_3,
  input  [15:0] in_4,
  input  [15:0] in_5,
  input  [15:0] in_6,
  input  [15:0] in_7,
  input  [15:0] in_8,
  output out_9,
  output out_10,
  output out_11,
  output out_12,
  output out_13,
  output out_14,
  output out_15,
  output out_16,
  output out_17,
  output out_18,
  output out_19,
  output out_20
);

  Comparator16Bit comparator16bit_1 (.A(in_1), .B(in_3), .Less(out_13), .Great(out_9), .Equal(out_11));
  Comparator16Bit comparator16bit_2 (.A(in_6), .B(in_8), .Less(out_20), .Great(out_16), .Equal(out_18));
  Comparator16Bit comparator16bit_3 (.A(in_2), .B(in_4), .Less(out_14), .Great(out_10), .Equal(out_12));
  Comparator16Bit comparator16bit_4 (.A(in_5), .B(in_7), .Less(out_19), .Great(out_15), .Equal(out_17));
endmodule

module testALU (
  input  [15:0] in_1,
  input  [15:0] in_2,
  input  [15:0] in_3,
  input  [15:0] in_4,
  input  [2:0] in_5,
  input  [2:0] in_6,
  input  [15:0] in_7,
  input  [15:0] in_8,
  input  [15:0] in_9,
  input  [15:0] in_10,
  input  [2:0] in_11,
  input  [2:0] in_12,
  output out_13,
  output out_14,
  output out_15,
  output out_16,
  output out_17,
  output out_18,
  output out_19,
  output out_20,
  output [15:0] out_21,
  output [15:0] out_22,
  output out_23,
  output out_24,
  output out_25,
  output out_26,
  output out_27,
  output out_28,
  output out_29,
  output out_30,
  output [15:0] out_31,
  output [15:0] out_32
);

  ALU alu_1 (
    .Selector(in_5), .A(in_3), .B(in_1), .Result(out_21), .P(out_13), .Z(out_15), .N(out_17),
    .Overflow(out_19));
  ALU alu_2 (
    .Selector(in_11), .A(in_9), .B(in_7), .Result(out_31), .P(out_23), .Z(out_25), .N(out_27),
    .Overflow(out_29));
  ALU alu_3 (
    .Selector(in_6), .A(in_4), .B(in_2), .Result(out_22), .P(out_14), .Z(out_16), .N(out_18),
    .Overflow(out_20));
  ALU alu_4 (
    .Selector(in_12), .A(in_10), .B(in_8), .Result(out_32), .P(out_24), .Z(out_26), .N(out_28),
    .Overflow(out_30));
endmodule

module TestALU2 (
  input  [15:0] in_1,
  input  [15:0] in_2,
  input  [15:0] in_3,
  input  [15:0] in_4,
  input  [2:0] in_5,
  input  [2:0] in_6,
  input  [15:0] in_7,
  input  [15:0] in_8,
  input  [15:0] in_9,
  input  [15:0] in_10,
  input  [2:0] in_11,
  input  [2:0] in_12,
  output out_13,
  output out_14,
  output out_15,
  output out_16,
  output out_17,
  output out_18,
  output out_19,
  output out_20,
  output [15:0] out_21,
  output [15:0] out_22,
  output out_23,
  output out_24,
  output out_25,
  output out_26,
  output out_27,
  output out_28,
  output out_29,
  output out_30,
  output [15:0] out_31,
  output [15:0] out_32
);

  ALU alu_1 (
    .Selector(in_5), .A(in_3), .B(in_1), .Result(out_21), .P(out_13), .Z(out_15), .N(out_17),
    .Overflow(out_19));
  ALU alu_2 (
    .Selector(in_11), .A(in_9), .B(in_7), .Result(out_31), .P(out_23), .Z(out_25), .N(out_27),
    .Overflow(out_29));
  ALU alu_3 (
    .Selector(in_6), .A(in_4), .B(in_2), .Result(out_22), .P(out_14), .Z(out_16), .N(out_18),
    .Overflow(out_20));
  ALU alu_4 (
    .Selector(in_12), .A(in_10), .B(in_8), .Result(out_32), .P(out_24), .Z(out_26), .N(out_28),
    .Overflow(out_30));
endmodule

module testALU3 (
  input  [15:0] in_1,
  input  [15:0] in_2,
  input  [2:0] in_3,
  input  [2:0] in_4,
  output out_5,
  output out_6,
  output out_7,
  output out_8,
  output out_9,
  output out_10,
  output out_11,
  output out_12,
  output [15:0] out_13,
  output [15:0] out_14
);

  ALU alu_1 (.Selector(in_3), .A(in_2), .B(in_1), .Result(out_13), .P(out_5), .Z(out_7), .N(out_9), .Overflow(out_11));
  ALU alu_2 (.Selector(in_4), .A(in_2), .B(in_1), .Result(out_14), .P(out_6), .Z(out_8), .N(out_10), .Overflow(out_12));
endmodule

module testALU4 (
  input  [15:0] in_1,
  input  [15:0] in_2,
  input  [2:0] in_3,
  input  [2:0] in_4,
  input  [2:0] in_5,
  input  [2:0] in_6,
  output out_7,
  output out_8,
  output out_9,
  output out_10,
  output out_11,
  output out_12,
  output out_13,
  output out_14,
  output [15:0] out_15,
  output [15:0] out_16,
  output out_17,
  output out_18,
  output out_19,
  output out_20,
  output out_21,
  output out_22,
  output out_23,
  output out_24,
  output [15:0] out_25,
  output [15:0] out_26
);

  ALU alu_1 (.Selector(in_3), .A(in_2), .B(in_1), .Result(out_15), .P(out_7), .Z(out_9), .N(out_11), .Overflow(out_13));
  ALU alu_2 (
    .Selector(in_5), .A(in_2), .B(in_1), .Result(out_25), .P(out_17), .Z(out_19), .N(out_21),
    .Overflow(out_23));
  ALU alu_3 (
    .Selector(in_4), .A(in_2), .B(in_1), .Result(out_16), .P(out_8), .Z(out_10), .N(out_12), .Overflow(out_14));
  ALU alu_4 (
    .Selector(in_6), .A(in_2), .B(in_1), .Result(out_26), .P(out_18), .Z(out_20), .N(out_22),
    .Overflow(out_24));
endmodule

module norAnd (
  input  in_1,
  input  in_2,
  output out_3
);

  wire nor_1_out;

  nor nor_1 (nor_1_out, in_1, in_2);
  not nor_2 (out_3, nor_1_out);  // NOR_Gate
endmodule

module PriotyEncoder4to2 (
  input  I0,
  input  I1,
  input  I2,
  input  I3,
  output V,
  output Y0,
  output Y1
);

  wire and_1_out, not_1_out;

  not not_1 (not_1_out, I2);
  and and_1 (and_1_out, I1, not_1_out);
  or or_1 (V, I0, I1, I2, I3);
  or or_2 (Y0, and_1_out, I3);
  or or_3 (Y1, I2, I3);
endmodule

module TestEncoder (
  input  in_1,
  input  in_2,
  input  in_3,
  input  in_4,
  input  in_5,
  input  in_6,
  input  in_7,
  input  in_8,
  input  in_9,
  input  in_10,
  input  in_11,
  input  in_12,
  input  in_13,
  input  in_14,
  input  in_15,
  input  in_16,
  input  in_17,
  input  in_18,
  input  in_19,
  input  in_20,
  output out_21,
  output out_22,
  output out_23,
  output out_24,
  output out_25,
  output out_26,
  output out_27,
  output out_28,
  output out_29,
  output out_30,
  output out_31,
  output out_32,
  output out_33,
  output out_34,
  output out_35,
  output out_36,
  output out_37,
  output out_38,
  output out_39,
  output out_40,
  output out_41,
  output out_42,
  output out_43,
  output out_44,
  output out_45,
  output out_46,
  output out_47,
  output out_48,
  output out_49,
  output out_50
);

  PriotyEncoder4to2 priotyencoder4to2_1 (
    .I0(in_1), .I1(in_2), .I2(in_3), .I3(in_4), .V(out_21), .Y0(out_22), .Y1(out_25));
  PriotyEncoder4to2 priotyencoder4to2_2 (
    .I0(in_5), .I1(in_6), .I2(in_7), .I3(in_8), .V(out_27), .Y0(out_28), .Y1(out_31));
  PriotyEncoder4to2 priotyencoder4to2_3 (
    .I0(in_9), .I1(in_10), .I2(in_11), .I3(in_12), .V(out_33), .Y0(out_34), .Y1(out_37));
  PriotyEncoder4to2 priotyencoder4to2_4 (
    .I0(in_13), .I1(in_14), .I2(in_15), .I3(in_16), .V(out_39), .Y0(out_40), .Y1(out_43));
  PriotyEncoder4to2 priotyencoder4to2_5 (
    .I0(in_17), .I1(in_18), .I2(in_19), .I3(in_20), .V(out_45), .Y0(out_46), .Y1(out_49));
  Priority_Encoder #(.select(2)) priority_encoder_1 (
    .in0(in_1), .in1(in_2), .in2(in_3), .in3(in_4), .out({out_24, out_23}), .gs(out_26));  // open: en_out, en_in
  Priority_Encoder #(.select(2)) priority_encoder_2 (
    .in0(in_5), .in1(in_6), .in2(in_7), .in3(in_8), .out({out_30, out_29}), .gs(out_32));  // open: en_out, en_in
  Priority_Encoder #(.select(2)) priority_encoder_3 (
    .in0(in_9), .in1(in_10), .in2(in_11), .in3(in_12), .out({out_36, out_35}), .gs(out_38));  // open: en_out, en_in
  Priority_Encoder #(.select(2)) priority_encoder_4 (
    .in0(in_13), .in1(in_14), .in2(in_15), .in3(in_16), .out({out_42, out_41}), .gs(out_44));  // open: en_out, en_in
  Priority_Encoder #(.select(2)) priority_encoder_5 (
    .in0(in_17), .in1(in_18), .in2(in_19), .in3(in_20), .out({out_48, out_47}), .gs(out_50));  // open: en_out, en_in
endmodule

module myOR (
  input  in_1,
  input  in_2,
  output out_3
);

  wire nor_1_out;

  nor nor_1 (nor_1_out, in_1, in_2);
  nor nor_2 (out_3, nor_1_out, nor_1_out);

  // Notes on the sheet:
  //   OR
endmodule

module myAND (
  input  in_1,
  input  in_2,
  output out_3
);

  wire nand_1_out;

  nand nand_1 (nand_1_out, in_1, in_2);
  nand nand_2 (out_3, nand_1_out, nand_1_out);

  // Notes on the sheet:
  //   AND
endmodule

module MyNOT (
  input  in_1,
  output out_2
);

  nand nand_1 (out_2, in_1, in_1);
endmodule

module Exercise1 (
  input  A,
  input  B,
  input  C,
  input  D,
  output out_5
);

  wire myand_1_out_3, myand_2_out_3, myand_3_out_3, myand_4_out_3, myand_5_out_3, mynot_1_out_2,
       mynot_2_out_2, mynot_3_out_2, myor_1_out_3;

  MyNOT mynot_1 (.in_1(A), .out_2(mynot_1_out_2));
  MyNOT mynot_2 (.in_1(C), .out_2(mynot_2_out_2));
  myAND myand_1 (.in_1(mynot_1_out_2), .in_2(B), .out_3(myand_1_out_3));
  myAND myand_2 (.in_1(mynot_2_out_2), .in_2(A), .out_3(myand_2_out_3));
  MyNOT mynot_3 (.in_1(D), .out_2(mynot_3_out_2));
  myAND myand_3 (.in_1(A), .in_2(D), .out_3(myand_3_out_3));
  myAND myand_4 (.in_1(myand_1_out_3), .in_2(mynot_2_out_2), .out_3(myand_4_out_3));
  myAND myand_5 (.in_1(myand_2_out_3), .in_2(mynot_3_out_2), .out_3(myand_5_out_3));
  myOR myor_1 (.in_1(myand_4_out_3), .in_2(myand_5_out_3), .out_3(myor_1_out_3));
  myOR myor_2 (.in_1(myor_1_out_3), .in_2(myand_3_out_3), .out_3(out_5));
endmodule

module Exercise1simple (
  input  A,
  input  B,
  input  C,
  input  D,
  output F
);

  wire myand_1_out_3, myand_2_out_3, myand_3_out_3, mynot_1_out_2, myor_1_out_3;

  MyNOT mynot_1 (.in_1(C), .out_2(mynot_1_out_2));
  myAND myand_1 (.in_1(A), .in_2(mynot_1_out_2), .out_3(myand_1_out_3));
  myAND myand_2 (.in_1(B), .in_2(mynot_1_out_2), .out_3(myand_2_out_3));
  myAND myand_3 (.in_1(D), .in_2(A), .out_3(myand_3_out_3));
  myOR myor_1 (.in_1(myand_1_out_3), .in_2(myand_2_out_3), .out_3(myor_1_out_3));
  myOR myor_2 (.in_1(myor_1_out_3), .in_2(myand_3_out_3), .out_3(F));
endmodule
